// Logisim project ex1_ex2.circ as structural Verilog: 1 circuit, main circuit main
module main (
);

  wire n7408_1_pin8, n7408_1_pin11, n7486_1_pin1, n7486_1_pin2, n7486_1_pin3, n7486_1_pin8, n7486_1_pin9,
       n7486_1_pin11;

  _7486 u_7486_1 (
    .pin1(n7486_1_pin1), .pin2(n7486_1_pin2), .pin3(n7486_1_pin3), .pin13(n7486_1_pin1),
    .pin12(n7486_1_pin2), .pin11(n7486_1_pin11), .pin10(n7486_1_pin11), .pin9(n7486_1_pin9),
    .pin8(n7486_1_pin8));  // open: pin4, pin5, pin6
  _7408 u_7408_1 (
    .pin13(n7486_1_pin1), .pin12(n7486_1_pin2), .pin11(n7408_1_pin11), .pin10(n7408_1_pin11),
    .pin9(n7486_1_pin3), .pin8(n7408_1_pin8));  // open: pin1, pin2, pin3, pin4, pin5, pin6

  // Notes on the sheet:
  //   A
  //   B
  //   Cin
endmodule
